# Fritzing sketch nabukeys (saved by Fritzing 0.9.3b)
circuit board: 6.88566cm x 5.36311cm
breadboards: 1

parts:
  PCB1 = Arduino Shield PCB  # not connected
  J11 = female pin header, 8 pins [form="♀ (female)"]
  J12 = female pin header, 6 pins [form="♀ (female)"]
  J13 = female pin header, 8 pins [form="♀ (female)"]
  J14 = female pin header, 10 pins [form="♀ (female)"]
  S15 = Toggle Switch [package=THT]
  S16 = Toggle Switch [package=THT]
  S17 = Toggle Switch [package=THT]
  S18 = Toggle Switch [package=THT]
  S19 = Pushbutton [package="[THT]"]
  R1 = Resistor [tolerance=±5% resistance=10k package=THT]
  C1 = Ceramic Capacitor [capacitance=1nF package="100 mil [THT, multilayer]"]
  C2 = Ceramic Capacitor [capacitance=1nF package="100 mil [THT, multilayer]"]
  SN75176AP = IC, DIP package, 8 pins [chip_label=IC]
  IRLU110PBF = Basic FET N-Channel [package="TO220 [THT]"]
  R2 = Resistor [tolerance=±5% resistance=180 package=THT]
  S20 = Toggle Switch [package=THT]
  S21 = Toggle Switch [package=THT]
  J15 = female pin header, 1 pin [form="♀ (female)"]  # not connected
  J16 = female pin header, 1 pin [form="♀ (female)"]
  J17 = female pin header, 1 pin [form="♀ (female)"]
  J18 = female pin header, 1 pin [form="♀ (female)"]
  J19 = female pin header, 1 pin [form="♀ (female)"]  # not connected
  J20 = female pin header, 1 pin [form="♀ (female)"]
  J21 = female pin header, 1 pin [form="♀ (female)"]
  J22 = female pin header, 1 pin [form="♀ (female)"]
  J23 = female pin header, 1 pin [form="♀ (female)"]
  J24 = female pin header, 1 pin [form="♀ (female)"]

nets:
  N1: J11.pin3, SN75176AP.pin4
  N2: J11.pin4, SN75176AP.pin2, SN75176AP.pin3
  N3: J11.pin5, SN75176AP.pin1
  N4: J11.pin6, R1.Pin_0, IRLU110PBF.gate
  N5: J12.pin1, S18.L2
  N6: J12.pin2, S17.L2
  N7: J12.pin3, S16.L2
  N8: J12.pin4, S15.L2
  N9: J12.pin5, S21.L2
  N10: J12.pin6, S20.L2
  N11: J13.pin3, S19.Pin_1, S19.Pin_2
  N12: J13.pin5, SN75176AP.pin8
  N13: J13.pin6, J13.pin7, J14.pin4, S15.L1, S15.COM, S16.L1, S16.COM, S17.L1, S17.COM, S18.L1, S18.COM, S19.Pin_3, S19.Pin_4, R1.Pin_1, C1.1, C2.0, SN75176AP.pin5, IRLU110PBF.source, S20.L1, S20.COM, S21.L1, S21.COM, J21.pin1, J22.pin1, J23.pin1, J24.pin1
  N14: J13.pin8, J16.pin1
  N15: C1.0, SN75176AP.pin7, R2.Pin_1, J20.pin1
  N16: C2.1, SN75176AP.pin6, R2.Pin_0, J17.pin1
  N17: IRLU110PBF.drain, J18.pin1

notes:
  >NH
  NK>
  USB
  SER
  A
  B
  C
  D
  RESET
  5-B
  4-A
  3-VIN
  2-RET
  1-NC
  Tester/
  Translator/
  Emulator
  Keyboard
  2-Q1
  3-R/RX
  4-DE/#RE
  5-D/TX
  MOST OF THE COMPUTERS
  ARE SEEEEEEEEWWWWWWWW
  STEEEEEEWWWWWWPIIIIID
  E
  F
  -----------
  ------ ------
  -------------

custom parts:
  Arduino Shield PCB: Plain PCB Shaped to fit an Arduino "Shield"
